// Logisim project calc.circ as structural Verilog: 1 circuit, main circuit main
module main (
  input  _1,
  input  _2,
  input  _3,
  input  _1_2,
  input  _2_2,
  input  _3_2,
  output out_7,
  output out_8,
  output out_9
);

  wire and_1_out, and_2_out, and_3_out, and_4_out, and_5_out, and_6_out, and_7_out, and_9_out, and_10_out,
       and_11_out, and_12_out, and_14_out, and_15_out, and_16_out, and_17_out, and_18_out, button_1_out,
       button_2_out, button_3_out, button_4_out, button_5_out, button_6_out, button_7_out, not_1_out,
       not_2_out, not_3_out, not_4_out, not_5_out, not_6_out, not_7_out, not_8_out, not_9_out, not_10_out,
       not_11_out, not_12_out, not_13_out, not_14_out, not_15_out, or_1_out, or_2_out, or_3_out, or_4_out,
       or_6_out, or_7_out, or_8_out, or_9_out, or_10_out, or_11_out, or_12_out, or_14_out, or_15_out,
       or_16_out;

  or or_1 (or_1_out, _3, _2);
  or or_2 (or_2_out, or_3_out, or_7_out);
  and and_1 (and_1_out, or_3_out, or_7_out);
  or or_3 (or_3_out, _3, _1);
  not not_1 (not_1_out, and_1_out);
  not not_2 (not_2_out, and_2_out);
  and and_2 (and_2_out, and_1_out, or_1_out);
  and and_3 (and_3_out, and_1_out, or_1_out);
  and and_4 (and_4_out, and_1_out, or_4_out);
  and and_5 (and_5_out, or_4_out, or_1_out);
  or or_4 (or_4_out, _3_2, _2_2);
  and and_6 (and_6_out, and_1_out, not_2_out);
  and and_7 (and_7_out, not_2_out, or_1_out);
  or or_5 (out_7, and_3_out, or_6_out);
  or or_6 (or_6_out, and_4_out, and_5_out);
  or or_7 (or_7_out, _3_2, _1_2);
  and and_8 (out_9, or_2_out, not_1_out);
  or or_8 (or_8_out, and_6_out, and_7_out);
  not not_3 (not_3_out, out_7);
  not not_4 (not_4_out, out_8);
  not not_5 (not_5_out, out_9);
  Button button_1 (.out(button_1_out));
  and and_9 (and_9_out, not_3_out, not_4_out, not_5_out);
  or or_9 (or_9_out, and_12_out, and_9_out, and_17_out, button_1_out, and_18_out);
  Button button_2 (.out(button_2_out));
  and and_10 (and_10_out, out_9, not_6_out, not_7_out);
  not not_6 (not_6_out, out_8);
  not not_7 (not_7_out, out_7);
  or or_10 (or_10_out, and_17_out, and_16_out, and_9_out, button_2_out);
  Button button_3 (.out(button_3_out));
  not not_8 (not_8_out, out_9);
  not not_9 (not_9_out, out_7);
  or or_11 (or_11_out, and_9_out, and_17_out, and_12_out, button_3_out, and_18_out);
  _7_Segment_Display u_7_segment_display_1 (
    .g(or_9_out), .f(or_10_out), .a(or_11_out), .b(or_12_out), .e(or_16_out), .d(or_15_out), .c(or_14_out));  // open: dp
  and and_11 (and_11_out, or_8_out, or_4_out);
  and and_12 (and_12_out, not_8_out, out_8, not_9_out);
  or or_12 (or_12_out, and_9_out, and_9_out, and_9_out, and_12_out, and_9_out, button_4_out, and_18_out, and_10_out);
  Button button_4 (.out(button_4_out));
  not not_10 (not_10_out, and_11_out);
  and and_13 (and_9_out, out_9, out_8, not_11_out);
  not not_11 (not_11_out, out_7);
  and and_14 (and_14_out, or_8_out, not_10_out);
  and and_15 (and_15_out, not_10_out, or_4_out);
  not not_12 (not_12_out, out_8);
  not not_13 (not_13_out, out_9);
  Button button_5 (.out(button_5_out));
  or or_13 (out_8, and_14_out, and_15_out);
  not not_14 (not_14_out, out_8);
  and and_16 (and_16_out, not_12_out, not_13_out, out_7);
  or or_14 (or_14_out, and_16_out, and_16_out, and_9_out, and_10_out, and_9_out, and_17_out);
  Button button_6 (.out(button_6_out));
  and and_17 (and_17_out, out_7, not_14_out, out_9);
  or or_15 (or_15_out, and_17_out, and_9_out, and_12_out, and_9_out, button_6_out);
  Button button_7 (.out(button_7_out));
  and and_18 (and_18_out, out_7, out_8, not_15_out);
  not not_15 (not_15_out, out_9);
  or or_16 (or_16_out, and_12_out, and_9_out, button_7_out);
endmodule
